# Fritzing sketch proiektua sigelineas USTEZ FINALA (saved by Fritzing 0.9.3b)
breadboards: 1

parts:
  Componente1 = iceZUM Alhambra
  M1 = DC Motor
  M2 = DC Motor
  U1 = LM2596 step down module
  Q1 = PHOTOTRANSISTOR REFLECTIVE OBJECT SENSOR [package=qrb1114-side]
  Q2 = PHOTOTRANSISTOR REFLECTIVE OBJECT SENSOR [package=qrb1114-side]
  R1 = Resistor [tolerance=±5% resistance=220 package=THT]
  R2 = Resistor [tolerance=±5% resistance=220 package=THT]
  R3 = Resistor [tolerance=±5% resistance=220 package=THT]
  R6 = Resistor [tolerance=±5% resistance=220 package=THT]
  X1 = USB Connectors [package=usb-minib-old]
  VCC1 = Battery block 9V
  Q3 = PHOTOTRANSISTOR REFLECTIVE OBJECT SENSOR [package=qrb1114-side]
  Q4 = PHOTOTRANSISTOR REFLECTIVE OBJECT SENSOR [package=qrb1114-side]
  R7 = Resistor [tolerance=±5% resistance=220 package=THT]
  R8 = Resistor [tolerance=±5% resistance=220 package=THT]
  R9 = Resistor [tolerance=±5% resistance=220 package=THT]
  R10 = Resistor [tolerance=±5% resistance=220 package=THT]
  Componente2 = Motor Driver 1A Dual TB6612FNG
  D1 = Zener Diode [part_number=1N4732A breakdown_voltage=3.6V package="300 mil [THT]"]
  D2 = Rectifier Diode [part_number=1N4001 package="300 mil [THT]"]  # not connected
  LED1 = smd LED [color="Red (633nm)" package="1206 [SMD]"]
  R11 = Resistor [tolerance=±5% resistance=220 package=THT]
  Q5 = NPN-Transistor [package="TO92 [THT]"]
  D3 = Zener Diode [part_number=1N4732A breakdown_voltage=5.1V package="300 mil [THT]"]

nets:
  N1: Componente1.D1, Componente1.V1, Componente2.STBY
  N2: Componente1.D4, Componente1.V4, Q2.C, R2.Pin_1
  N3: Componente1.D5, Componente1.V5, Q1.C, R1.Pin_1
  N4: Componente1.D6, Componente1.D7, Componente1.V7, Componente1.V6, Q3.E, R10.Pin_0
  N5: Componente1.D8, Componente1.V8, Componente2.PWMA
  N6: Componente1.D9, Componente2.PWMB
  N7: Componente1.D10, Componente2.AIN1
  N8: Componente1.D11, Componente2.AIN2
  N9: Componente1.D12, Componente2.BIN1
  N10: Componente1.D13, Componente2.BIN2
  GND: Componente1.GD2, Componente1.GND, U1.IN-, U1.OUT-, R1.Pin_0, R2.Pin_0, R3.Pin_1, R6.Pin_1, VCC1.-, R7.Pin_0, R8.Pin_0, R9.Pin_1, R10.Pin_1, Componente2.GND, LED1.anode, D3.anode
  N11: Componente1.5V, M1.pin_1, M2.pin_1, M2.pin_2, Q1.A, Q1.K, Q2.A, Q2.K, Q3.A, Q3.K, Q4.A, Q4.K, Componente2.B01, Componente2.B02, Componente2.A01
  N12: M1.pin_2, Componente2.A02
  N13: U1.IN+, VCC1.+, D1.cathode, R11.Pin_0, Q5.E
  N14: U1.OUT+, Componente2.VM
  N15: Q1.E, R3.Pin_0
  N16: Q2.E, R6.Pin_0
  N17: X1.D-, Componente2.VCC, Q5.C
  N18: Q3.C, R9.Pin_0
  N19: Q4.C, R8.Pin_1
  N20: Q4.E, R7.Pin_1
  N21: R11.Pin_1, Q5.B, D3.cathode

custom parts:
  iceZUM Alhambra: Arduino/zum compatible Open FPGA electronic board. Synthesize hardware easily, using only open source tools
  LM2596 step down module: LM2596 DC-DC step down power supply module 3 A.
